# Fritzing sketch A00020-PART-01-FRITZ-Sketch (saved by Fritzing 0.9.10b)
stripboards: 1

parts:
  U1 = ESP32S-HiLetgo [part_number=ESP32S-HiLetgo]
  Compass1 = Compass [form="long pad" package=THT]
  GYRO1 = GYRO [form="♂ (male)" package=THT]
  Hall_Effect1 = Hall effect sensor [package="TO92 [THT]"]  # not connected
  R1 = Resistor [tolerance=±5% power=0.25 resistance=220 package=THT]  # not connected

nets:
  GND: U1.GND, Compass1.GND, GYRO1.GND
  VCC: U1.VIN, Compass1.VCC, GYRO1.VCC
  N1: U1.GPIO21, Compass1.SDA, GYRO1.SDA
  N2: U1.GPIO22, Compass1.SCL, GYRO1.SCL
  N3: Compass1.DRDY, GYRO1.XDA

notes:
  Cut traces here:

custom parts:
  ESP32S-HiLetgo: HiLetgo ESP-WROOM-32 ESP32 ESP-32S Development Board 2.4GHz Dual-Mode WiFi + Bluetooth Dual Cores Microcontroller The ESP32 integrated with Antenna switches, RF Balun, power amplifiers, low-noise amplifiers, filters, and management modules, and the entire solution occupies the least area of PCB. 2.4 GHz Wi-Fi plus Bluetooth dual-mode chip, with TSMC Ultra-low power consumption 40nm technology,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
